# Fritzing sketch trixie-digital-gauge (saved by Fritzing 0.9.3b)

parts:
  Part1 = Adafruit Perma-Proto HAT [part_number="Adafruit #2314 and #2310"]
  Part2 = OLED Color 1.5 inch 128x128 w microSD [part_number=1431]

nets:
  N1: Part1.SPI_MOSI, Part2.MOSI
  N2: Part1.SPI_MISO, Part2.SD_MISO
  N3: Part1.SPI_SCLK, Part2.SCK
  3.3V: Part1.3.3V, Part2.3.3V
  GND: Part1.GND, Part2.GND

custom parts:
  Adafruit Perma-Proto HAT: To kick off the Adafruit HAT party, we have this Perma-Proto inspired plug in daughter board. It has a grid of 0.1" prototyping soldering holes for attaching chips, resistors, LED, potentiometers and more. The holes are connected underneath with traces to mimic the solderless breadboards you're familiar. There's also long power strips for +3V, +5V and Ground connections to the Pi. Near the top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
  OLED Color 1.5 inch 128x128 w microSD: The visible portion of this OLED measures 1.5" diagonal and contains 128x128 RGB pixels, each one made of red, green and blue OLEDs. Each pixel can be set with 16-bits of resolution for a large range of colors. Because the display uses OLEDs, there is no backlight, and the contrast is very high (black is really black). We picked this display for its excellent color, this is the nicest mini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
